# Fritzing sketch MIDIPixelBoard R10 (saved by Fritzing 0.9.3b)
circuit board: 8.27736cm x 5.15512cm
breadboards: 1

parts:
  MIDI_Processor = Arduino Nano (Rev3.0)
  NeoPixel_Controller = Arduino Nano (Rev3.0)
  R1 = Resistor [tolerance=±5% resistance=470 package=THT]
  R2 = Resistor [tolerance=±5% resistance=470 package=THT]
  Power_In = Screw terminal - 2 pins [package=THT]
  Right_Data = Screw terminal - 2 pins [package=THT]
  Left_Data = Screw terminal - 2 pins [package=THT]
  Left_Power = Screw terminal - 2 pins [package=THT]
  Right_Power = Screw terminal - 2 pins [package=THT]
  Sensors = male pin header, 9 pins [form="♂ (male)"]
  Data = male pin header, 3 pins [form="♂ (male)"]
  C1 = Electrolytic Capacitor [capacitance=1mF package="100 mil [THT, electrolytic]"]

nets:
  N1: MIDI_Processor.D1/TX, Data.pin1
  N2: MIDI_Processor.D0/RX, Data.pin2
  GND: MIDI_Processor.GND, NeoPixel_Controller.GND, Power_In.pin2, Right_Data.pin2, Left_Data.pin2, Left_Power.pin2, Right_Power.pin2, Sensors.pin9, Data.pin3, C1.-
  N3: MIDI_Processor.D2, Sensors.pin8
  N4: MIDI_Processor.D3, Sensors.pin7
  N5: MIDI_Processor.D4, Sensors.pin6
  N6: MIDI_Processor.D5, Sensors.pin5
  N7: MIDI_Processor.D8, NeoPixel_Controller.D9
  N8: MIDI_Processor.D9, NeoPixel_Controller.D8
  N9: MIDI_Processor.D10, NeoPixel_Controller.D10
  PWR: MIDI_Processor.VIN, Power_In.pin1, Left_Power.pin1, Right_Power.pin1, C1.+
  5V: MIDI_Processor.5V, NeoPixel_Controller.5V
  N10: MIDI_Processor.A3, Sensors.pin4
  N11: MIDI_Processor.A2, Sensors.pin3
  N12: MIDI_Processor.A1, Sensors.pin2
  N13: MIDI_Processor.A0, Sensors.pin1
  N14: NeoPixel_Controller.D11/MOSI, R1.Pin_0
  N15: NeoPixel_Controller.D12/MISO, R2.Pin_0
  N16: R1.Pin_1, Right_Data.pin1
  N17: R2.Pin_1, Left_Data.pin1

notes:
  Cyborg Sensor Audio Visual Controller
  USB
  Arduino Nano 1
  Arduino Nano 2
  A0
  A1
  A2
  A3
  D5
  D4
  D3
  D2
  GND
  Tx
  Rx
  NeoPixel Controller
  Schema Factor 2017
  0v2
  -
  +
  MIDI Processor
