# Fritzing sketch MIDIPixelBoard (saved by Fritzing 0.9.3b)
circuit board: 8.14442cm x 5.34797cm
breadboards: 1

parts:
  MIDI_Processor = Arduino Nano (Rev3.0)
  NeoPixel_Controller = Arduino Nano (Rev3.0)
  R1 = Resistor [tolerance=±5% resistance=330 package=THT]
  R2 = Resistor [tolerance=±5% resistance=330 package=THT]
  Power_In = Screw terminal - 2 pins [package=THT]
  Right_Data = Screw terminal - 2 pins [package=THT]
  Left_Data = Screw terminal - 2 pins [package=THT]
  Left_Power = Screw terminal - 2 pins [package=THT]
  Right_Power = Screw terminal - 2 pins [package=THT]
  Data = male pin header, 2 pins [form="♂ (male)"]
  Sensors = male pin header, 9 pins [form="♂ (male)"]

nets:
  N1: MIDI_Processor.D1/TX, Data.pin1
  N2: MIDI_Processor.D0/RX, Data.pin2
  GND: MIDI_Processor.GND, NeoPixel_Controller.GND, Power_In.pin2, Right_Data.pin2, Left_Data.pin2, Left_Power.pin2, Right_Power.pin2, Sensors.pin9
  N3: MIDI_Processor.D2, Sensors.pin8
  N4: MIDI_Processor.D3, Sensors.pin7
  N5: MIDI_Processor.D4, Sensors.pin6
  N6: MIDI_Processor.D5, Sensors.pin5
  N7: MIDI_Processor.D10, NeoPixel_Controller.D10
  PWR: MIDI_Processor.VIN, Power_In.pin1, Left_Power.pin1, Right_Power.pin1
  5V: MIDI_Processor.5V, NeoPixel_Controller.5V
  N8: MIDI_Processor.A5, Sensors.pin4
  N9: MIDI_Processor.A4, Sensors.pin3
  N10: MIDI_Processor.A3, Sensors.pin2
  N11: MIDI_Processor.A2, Sensors.pin1
  N12: MIDI_Processor.A1, NeoPixel_Controller.A0
  N13: MIDI_Processor.A0, NeoPixel_Controller.A1
  N14: NeoPixel_Controller.D12/MISO, R1.Pin_0
  N15: NeoPixel_Controller.D13/SCK, R2.Pin_0
  N16: R1.Pin_1, Right_Data.pin1
  N17: R2.Pin_1, Left_Data.pin1

notes:
  Cyborg Tactile Audio Visual Controller 0v1
  USB
  Arduino Nano
